// Logisim project ALU.circ as structural Verilog: 1 circuit, main circuit main
module main (
  input  Cin,
  input  [15:0] A,
  input  [15:0] B,
  input  [1:0] s1s0,
  input  Bin,
  input  [3:0] Dst,
  output [15:0] res,
  output cout,
  output equal
);

  wire comparator_1_lt;
  wire [15:0] adder_1_out, bit_extender_1_out, multiplexer_1_out, not_1_out, shifter_1_out;

  assign not_1_out = ~B;  // NOT_Gate not_1, 16 bits wide
  Multiplexer #(.width(16)) multiplexer_1 (.in0(B), .in1(not_1_out), .out(multiplexer_1_out), .sel(Bin));  // open: en
  Adder #(.width(16)) adder_1 (.a(A), .b(multiplexer_1_out), .out(adder_1_out), .cin(Cin), .cout(cout));
  Comparator #(.width(16)) comparator_1 (.a(A), .b(B), .eq(equal), .lt(comparator_1_lt));  // open: gt
  Shifter #(.width(16)) shifter_1 (.in(A), .\dist (Dst), .out(shifter_1_out));
  assign bit_extender_1_out = {{15{1'b0}}, comparator_1_lt};  // Bit_Extender bit_extender_1
  Multiplexer #(.select(2), .width(16)) multiplexer_2 (
    .in0(adder_1_out), .in1(bit_extender_1_out), .in2(shifter_1_out), .in3({16{1'b0}}), .out(res), .sel(s1s0));  // open: en
endmodule
