// Logisim project Processor.circ as structural Verilog: 3 circuits, main circuit main
module main (
  input  in_1,
  output [15:0] out_2,
  output [15:0] out_3,
  output [15:0] out_4,
  output Cout,
  output [9:0] out_6,
  output [15:0] out_7,
  output [15:0] out_8
);

  wire and_1_out, clock_1_out, control_unit_1_alu_source, control_unit_1_bin, control_unit_1_branch,
       control_unit_1_jump, control_unit_1_memory_read, control_unit_1_memory_write, control_unit_1_r_i,
       control_unit_1_reg_write, main_1_equal, not_1_out;
  wire [1:0] control_unit_1_alu_op, multiplexer_1_out;
  wire [3:0] bit_extender_2_out;
  wire [9:0] adder_1_out, bit_extender_1_out, bit_extender_3_out, multiplexer_2_out, multiplexer_3_out,
       register_1_q;
  wire [15:0] bit_extender_4_out, multiplexer_4_out;

  Register #(.width(10)) register_1 (.D(multiplexer_3_out), .Q(register_1_q), .clk(not_1_out), .clr(in_1));  // open: en
  not not_1 (not_1_out, clock_1_out);
  Clock clock_1 (.out(clock_1_out));
  Adder #(.width(10)) adder_1 (.a(10'h1), .b(register_1_q), .out(adder_1_out));  // open: cin, cout
  ROM #(.addrWidth(10), .dataWidth(10)) rom_1 (.addr(register_1_q), .data(out_6));  // open: sel
  assign bit_extender_1_out = {{3{1'b0}}, out_6[6:0]};  // Bit_Extender bit_extender_1
  assign bit_extender_2_out = {{3{1'b0}}, out_6[0]};  // Bit_Extender bit_extender_2
  Multiplexer #(.width(2)) multiplexer_1 (
    .in0(out_6[2:1]), .in1(out_6[4:3]), .out(multiplexer_1_out), .sel(control_unit_1_r_i));  // open: en
  Control_Unit control_unit_1 (
    .Opcode(out_6[9:7]), .ALU_op(control_unit_1_alu_op), .Jump(control_unit_1_jump),
    .Reg_Write(control_unit_1_reg_write), .Memory_Write(control_unit_1_memory_write),
    .ALU_Source(control_unit_1_alu_source), .Branch(control_unit_1_branch),
    .Memory_Read(control_unit_1_memory_read), .Bin(control_unit_1_bin), .R_I(control_unit_1_r_i));
  Multiplexer #(.width(10)) multiplexer_2 (
    .in0(adder_1_out), .in1(bit_extender_1_out), .out(multiplexer_2_out), .sel(control_unit_1_jump));  // open: en
  assign bit_extender_3_out = {{7{1'b0}}, out_6[2:0]};  // Bit_Extender bit_extender_3
  Multiplexer #(.width(10)) multiplexer_3 (
    .in0(multiplexer_2_out), .in1(bit_extender_3_out), .out(multiplexer_3_out), .sel(and_1_out));  // open: en
  Register_File register_file_1 (
    .Read_Data1(out_2), .Read_Data_2(out_8), .Write_Data(multiplexer_4_out),
    .Write_on_Registor(multiplexer_1_out), .Write(control_unit_1_reg_write), .Clock_Pulse(clock_1_out),
    .Read_Register_1(out_6[6:5]), .Read_Register_2(out_6[4:3]));
  assign bit_extender_4_out = {{6{1'b0}}, bit_extender_3_out};  // Bit_Extender bit_extender_4
  Multiplexer #(.width(16)) multiplexer_4 (
    .in0(out_4), .in1(out_7), .out(multiplexer_4_out), .sel(control_unit_1_memory_read));  // open: en
  Multiplexer #(.width(16)) multiplexer_5 (
    .in0(bit_extender_4_out), .in1(out_8), .out(out_3), .sel(control_unit_1_alu_source));  // open: en
  ALU_main main_1 (
    .Cin(control_unit_1_bin), .A(out_2), .B(out_3), .Bin(control_unit_1_bin), .Dst(bit_extender_2_out),
    .equal(main_1_equal), .s1s0(control_unit_1_alu_op), .res(out_4), .cout(Cout));
  and and_1 (and_1_out, control_unit_1_branch, main_1_equal);
  RAM #(.addrWidth(16), .dataWidth(16), .bus("separate")) ram_1 (
    .addr(out_4), .din(out_8), .data(out_7), .str(control_unit_1_memory_write), .clk(clock_1_out),
    .ld(control_unit_1_memory_read));  // open: sel, clr

  // Notes on the sheet:
  //   contents of rom_1 (hex, n*v repeats v):
  //   12 96
endmodule

module Register_File (
  input  [15:0] Write_Data,
  input  [1:0] Read_Register_1,
  input  [1:0] Write_on_Registor,
  input  [1:0] Read_Register_2,
  input  Write,
  input  Clock_Pulse,
  output [15:0] Read_Data1,
  output [15:0] Read_Data_2
);

  wire and_1_out, and_2_out, and_3_out, and_4_out, decoder_1_out0, decoder_1_out1, decoder_1_out2,
       decoder_1_out3;
  wire [15:0] register_1_q, register_2_q, register_3_q, register_4_q;

  Decoder #(.select(2)) decoder_1 (
    .out0(decoder_1_out0), .out1(decoder_1_out1), .out2(decoder_1_out2), .out3(decoder_1_out3),
    .sel(Write_on_Registor));  // open: en
  and and_1 (and_1_out, decoder_1_out0, Write);
  and and_2 (and_2_out, decoder_1_out1, Write);
  and and_3 (and_3_out, decoder_1_out2, Write);
  and and_4 (and_4_out, decoder_1_out3, Write);
  Register #(.width(16)) register_1 (.D(Write_Data), .en(and_1_out), .Q(register_1_q), .clk(Clock_Pulse));  // open: clr
  Register #(.width(16)) register_2 (.D(Write_Data), .en(and_2_out), .Q(register_2_q), .clk(Clock_Pulse));  // open: clr
  Register #(.width(16)) register_3 (.D(Write_Data), .en(and_3_out), .Q(register_3_q), .clk(Clock_Pulse));  // open: clr
  Register #(.width(16)) register_4 (.D(Write_Data), .en(and_4_out), .Q(register_4_q), .clk(Clock_Pulse));  // open: clr
  Multiplexer #(.select(2), .width(16)) multiplexer_1 (
    .in0(register_1_q), .in1(register_2_q), .in2(register_3_q), .in3(register_4_q), .out(Read_Data1),
    .sel(Read_Register_1));  // open: en
  Multiplexer #(.select(2), .width(16)) multiplexer_2 (
    .in0(register_1_q), .in1(register_2_q), .in2(register_3_q), .in3(register_4_q), .out(Read_Data_2),
    .sel(Read_Register_2));  // open: en
endmodule

module Control_Unit (
  input  [2:0] Opcode,
  output [1:0] ALU_op,
  output Jump,
  output Reg_Write,
  output Memory_Write,
  output ALU_Source,
  output Branch,
  output Memory_Read,
  output R_I,
  output Bin
);

  wire decoder_1_out0, decoder_1_out2, decoder_1_out3, or_1_out;

  Decoder #(.select(3)) decoder_1 (
    .out0(decoder_1_out0), .out1(Bin), .out2(decoder_1_out2), .out3(decoder_1_out3), .out4(Memory_Read),
    .out5(Memory_Write), .out6(Branch), .out7(Jump), .sel(Opcode));  // open: en
  Multiplexer #(.width(2)) multiplexer_1 (.in0(2'b00), .in1(Opcode[2:1]), .out(ALU_op), .sel(or_1_out));  // open: en
  or or_1 (or_1_out, decoder_1_out0, Bin, decoder_1_out2, decoder_1_out3);
  or or_2 (Reg_Write, Memory_Read, decoder_1_out0, Bin, decoder_1_out2, decoder_1_out3);
  or or_3 (ALU_Source, decoder_1_out0, Branch, Bin);
  or or_4 (R_I, Memory_Read, Memory_Write, Branch, decoder_1_out3);
endmodule
